# Fritzing sketch diagrama (saved by Fritzing 0.9.3b)

parts:
  Componente1 = Arduino Mega 2560 (Rev3)
  U3 = L298 [package=multiwatt15]
  hc-sr1 = hc-sr04
  J1 = Infrared Proximity Sensor
  M1 = DC Motor
  U4 = ESP8266 WiFi Module [part_number=ESP8266]
  M2 = DC Motor
  M3 = DC Motor
  M4 = DC Motor
  J2 = Infrared Proximity Sensor
  J3 = Infrared Proximity Sensor
  BAT1 = BC9VPC [package=bc9vpc]

nets:
  GND: Componente1.GND, hc-sr1.GND, J1.GND, U4.GND, J2.GND
  N1: Componente1.D13_PWM, U4.RXD
  N2: Componente1.D12_PWM, U4.TXD
  N3: Componente1.D9_PWM, U3.ENB
  N4: Componente1.D8_PWM, U3.ENA
  3V3: Componente1.3V3, U4.VCC
  VCC: Componente1.5V, hc-sr1.VCC, J1.Vcc, J2.Vcc, J3.Vcc
  N5: Componente1.D2_PWM, hc-sr1.Trig
  N6: Componente1.D3_PWM, hc-sr1.Echo
  N7: Componente1.D5_PWM, J3.Vout
  N8: Componente1.D6_PWM, J2.Vout
  N9: Componente1.D7_PWM, J1.Vout
  N10: Componente1.D22, U3.IN3
  N11: Componente1.D23, U3.IN4
  N12: Componente1.D24, U3.IN1
  N13: Componente1.D25, U3.IN2
  N14: U3.OUT1, M1.pin_2, M4.pin_2
  N15: U3.OUT2, M1.pin_1, M4.pin_1
  N16: U3.GND, BAT1.V-
  N17: U3.VLS, BAT1.V+
  N18: U3.OUT3, M2.pin_2, M3.pin_2
  N19: U3.OUT4, M2.pin_1, M3.pin_1
