# Fritzing sketch proyecto2 (saved by Fritzing 0.9.3b)

parts:
  Componente1 = Arduino Mega 2560 (Rev3)
  U1 = ESP8266 WiFi Module [part_number=ESP8266]
  hc-sr1 = hc-sr04
  U2 = MLX90614 [package=to-39]
  U4 = LCD-16X2 [package=lcd-16x2]  # not connected
  S1 = Round Pushbutton
  Componente2 = Real Time Clock Module - DS1307 RTC Breakout Board
  U6 = RELAY [package=relay-g5q]
  U7 = RELAY [package=relay-g5q]
  M2 = DC Motor
  microSD_Transflash1 = SparkFun - microSD Transflash
  U8 = BUTTONPAD-4X4 [package=buttonpad-4x4-special]
  SP1 = SPEAKER [package=pcb_mount_speaker]
  Componente3 = LED Matrix - Serial Interface - Red/Green/Blue
  L2 = Solenoid  # not connected

nets:
  N1: Componente1.A0, S1.leg0
  N2: Componente1.D21/SCL, U2.SCL_VZ
  N3: Componente1.D20/SDA, U2.PWM_SDA
  N4: Componente1.D19/RX1, U1.TXD
  N5: Componente1.D18/TX1, U1.RXD
  GND: Componente1.GND, hc-sr1.GND, microSD_Transflash1.GND
  N6: Componente1.D12_PWM, microSD_Transflash1.SCK
  N7: Componente1.D11_PWM, microSD_Transflash1.DI
  N8: Componente1.D10_PWM, Componente2.SQW
  N9: Componente1.D9_PWM, Componente2.SCL
  N10: Componente1.D8_PWM, Componente2.SDA
  3V3: Componente1.3V3, U1.VCC
  5V: Componente1.5V, microSD_Transflash1.VCC
  N11: Componente1.D2_PWM, U6.COIL2
  N12: Componente1.D3_PWM, U7.COIL2
  N13: Componente1.D4_PWM, Componente3.GND
  N14: Componente1.D6_PWM, hc-sr1.Trig
  N15: Componente1.D7_PWM, hc-sr1.Echo
  N16: Componente1.D22, U8.G$1_GND
  N17: Componente1.D24, U8.G$0_GRN
  N18: Componente1.D26, U8.G$0_BLU
  N19: Componente1.D28, U8.G$0_SIG1
  N20: Componente1.D30, U8.G$0_RED
  N21: Componente1.D32, U8.G$0_GND
  N22: Componente1.D34, U8.G$1_RED
  N23: Componente1.D36, U8.G$0_SIG2
  N24: U6.MAIN, U7.MAIN
  N25: U7.NO, M2.pin_2
  N26: microSD_Transflash1.CD, SP1.+
  N27: microSD_Transflash1.DO, SP1.-
